# Fritzing sketch Arduino and LCD Circuit (saved by Fritzing 0.9.3b)
breadboards: 1

parts:
  Part1 = Arduino Uno (Rev3) - ICSP
  Part2 = DeuLigne 1.1 - The Snootlab's LCD shield for Arduino
  LED1 = LED - 5mm [color="Red (633nm)" package="5 mm [THT]"]
  R1 = Resistor [tolerance=±5% resistance=220 package=THT]
  J1 = Piezo Speaker
  MIC1 = Microphone

nets:
  5V: Part1.5V, Part2.+5V
  N1: Part1.D13/SCK, MIC1.pin2
  GND: Part1.GND, Part2.GND, LED1.cathode, J1.pin2
  N2: Part1.AREF, J1.pin1, MIC1.pin1
  N3: Part1.D2, R1.Pin_0
  N4: Part1.RESET, Part2.RESET
  N5: LED1.anode, R1.Pin_1
