# Fritzing sketch simple led circuit (saved by Fritzing 0.9.3b)
circuit board: 2.77786cm x 2.09205cm
breadboards: 1

parts:
  R1 = Resistor [tolerance=±5% resistance=220 package=THT]
  LED1 = LED - 5mm [color="Red (633nm)" package="5 mm [THT]"]
  VCC1 = Battery

nets:
  N1: R1.Pin_0, VCC1.-
  N2: R1.Pin_1, LED1.cathode
  N3: LED1.anode, VCC1.+

notes:
  BJTM Technologies
